// Logisim project Car.circ as structural Verilog: 2 circuits, main circuit CarParts
module CarParts (
  input  en,
  input  [1:0] CarPart,
  output C0,
  output C1,
  output C2
);

  wire not_1_out;

  Multiplexer #(.select(2), .width(3)) multiplexer_1 (
    .in0(3'b101), .in1(3'b010), .in2(3'b111), .in3(3'b010), .out({C2, C1, C0}), .sel(CarPart), .en(en));
  assign {C2, C1, C0} = not_1_out ? 3'b000 : 3'bz;  // Controlled_Buffer controlled_buffer_1
  not not_1 (not_1_out, en);
endmodule

module Generator (
  input  en,
  input  clk,
  input  \generate ,
  input  [1:0] car_part,
  output [31:0] out_5
);

  wire [9:0] random_1_out;
  wire [30:1] carparts_1_c0;

  Random #(.width(10), .seed(1)) random_1 (.clk(clk), .next(\generate ), .out(random_1_out));  // open: clr
  CarParts carparts_1 (
    .en(random_1_out[0]), .CarPart(car_part), .C0(carparts_1_c0[1]), .C1(carparts_1_c0[2]),
    .C2(carparts_1_c0[3]));
  Multiplexer #(.width(32)) multiplexer_1 (
    .in0(32'h80000001), .in1({1'b1, carparts_1_c0, 1'b1}), .out(out_5), .sel(en));  // open: en
  CarParts carparts_2 (
    .en(random_1_out[1]), .CarPart(car_part), .C0(carparts_1_c0[4]), .C1(carparts_1_c0[5]),
    .C2(carparts_1_c0[6]));
  CarParts carparts_3 (
    .en(random_1_out[2]), .CarPart(car_part), .C0(carparts_1_c0[7]), .C1(carparts_1_c0[8]),
    .C2(carparts_1_c0[9]));
  CarParts carparts_4 (
    .en(random_1_out[3]), .CarPart(car_part), .C0(carparts_1_c0[10]), .C1(carparts_1_c0[11]),
    .C2(carparts_1_c0[12]));
  CarParts carparts_5 (
    .en(random_1_out[4]), .CarPart(car_part), .C0(carparts_1_c0[13]), .C1(carparts_1_c0[14]),
    .C2(carparts_1_c0[15]));
  CarParts carparts_6 (
    .en(random_1_out[5]), .CarPart(car_part), .C0(carparts_1_c0[16]), .C1(carparts_1_c0[17]),
    .C2(carparts_1_c0[18]));
  CarParts carparts_7 (
    .en(random_1_out[6]), .CarPart(car_part), .C0(carparts_1_c0[19]), .C1(carparts_1_c0[20]),
    .C2(carparts_1_c0[21]));
  CarParts carparts_8 (
    .en(random_1_out[7]), .CarPart(car_part), .C0(carparts_1_c0[22]), .C1(carparts_1_c0[23]),
    .C2(carparts_1_c0[24]));
  CarParts carparts_9 (
    .en(random_1_out[8]), .CarPart(car_part), .C0(carparts_1_c0[25]), .C1(carparts_1_c0[26]),
    .C2(carparts_1_c0[27]));
  CarParts carparts_10 (
    .en(random_1_out[9]), .CarPart(car_part), .C0(carparts_1_c0[28]), .C1(carparts_1_c0[29]),
    .C2(carparts_1_c0[30]));
endmodule
