// Logisim project Counters.circ as structural Verilog: 6 circuits, main circuit HAS
module HAS (
  input  Op1,
  input  Op0,
  input  Q0,
  input  CIn,
  output J,
  output K,
  output COut
);

  wire and_3_out, and_4_out, not_1_out, not_2_out;

  and and_1 (J, Op1, CIn);
  and and_2 (K, Op1, CIn);
  not not_1 (not_1_out, Op0);
  not not_2 (not_2_out, Q0);
  and and_3 (and_3_out, Op1, not_1_out, Q0, CIn);
  or or_1 (COut, and_3_out, and_4_out);
  and and_4 (and_4_out, Op1, Op0, not_2_out, CIn);
endmodule

module Conversor_D_JK (
  input  D,
  output J,
  output K
);

  not not_1 (K, D);

  assign J = D;
endmodule

module Counter_2_Bits (
  input  in_1,
  input  in_2,
  input  op0,
  input  op1,
  input  load,
  input  clk,
  input  en,
  input  _0,
  output out_9,
  output out_10,
  output out_11
);

  wire conversor_d_jk_1_j, conversor_d_jk_1_k, conversor_d_jk_2_j, conversor_d_jk_2_k, has_1_j, has_1_k,
       has_2_cout, has_2_j, has_2_k, multiplexer_1_out, multiplexer_2_out, multiplexer_3_out,
       multiplexer_4_out;

  HAS has_1 (.Op1(op1), .Op0(op0), .Q0(out_10), .CIn(has_2_cout), .J(has_1_j), .K(has_1_k), .COut(out_9));
  Multiplexer multiplexer_1 (.in0(has_1_k), .in1(conversor_d_jk_1_k), .out(multiplexer_1_out), .sel(load));  // open: en
  Conversor_D_JK conversor_d_jk_1 (.D(in_1), .J(conversor_d_jk_1_j), .K(conversor_d_jk_1_k));
  Multiplexer multiplexer_2 (.in0(has_1_j), .in1(conversor_d_jk_1_j), .out(multiplexer_2_out), .sel(load));  // open: en
  J_K_Flip_Flop j_k_ff_1 (
    .J(multiplexer_2_out), .clk(clk), .K(multiplexer_1_out), .Q(out_10), .en(en), .reset(_0));  // open: Qn, preset
  Multiplexer multiplexer_3 (.in0(has_2_k), .in1(conversor_d_jk_2_k), .out(multiplexer_3_out), .sel(load));  // open: en
  Conversor_D_JK conversor_d_jk_2 (.D(in_2), .J(conversor_d_jk_2_j), .K(conversor_d_jk_2_k));
  HAS has_2 (.Op1(op1), .Op0(op0), .Q0(out_11), .CIn(op1), .J(has_2_j), .K(has_2_k), .COut(has_2_cout));
  Multiplexer multiplexer_4 (.in0(has_2_j), .in1(conversor_d_jk_2_j), .out(multiplexer_4_out), .sel(load));  // open: en
  J_K_Flip_Flop j_k_ff_2 (
    .J(multiplexer_4_out), .clk(clk), .K(multiplexer_3_out), .Q(out_11), .en(en), .reset(_0));  // open: Qn, preset
endmodule

module Counter_3_Bits (
  input  in_1,
  input  in_2,
  input  in_3,
  input  op0,
  input  op1,
  input  load,
  input  clk,
  input  en,
  input  _0,
  output out_10,
  output out_11,
  output out_12,
  output out_13
);

  wire conversor_d_jk_1_j, conversor_d_jk_1_k, conversor_d_jk_2_j, conversor_d_jk_2_k, conversor_d_jk_3_j,
       conversor_d_jk_3_k, has_1_j, has_1_k, has_2_cout, has_2_j, has_2_k, has_3_cout, has_3_j, has_3_k,
       multiplexer_1_out, multiplexer_2_out, multiplexer_3_out, multiplexer_4_out, multiplexer_5_out,
       multiplexer_6_out;

  HAS has_1 (.Op1(op1), .Op0(op0), .Q0(out_11), .CIn(has_2_cout), .J(has_1_j), .K(has_1_k), .COut(out_10));
  Multiplexer multiplexer_1 (.in0(has_1_j), .in1(conversor_d_jk_1_j), .out(multiplexer_1_out), .sel(load));  // open: en
  Multiplexer multiplexer_2 (.in0(has_1_k), .in1(conversor_d_jk_1_k), .out(multiplexer_2_out), .sel(load));  // open: en
  Conversor_D_JK conversor_d_jk_1 (.D(in_1), .J(conversor_d_jk_1_j), .K(conversor_d_jk_1_k));
  J_K_Flip_Flop j_k_ff_1 (
    .J(multiplexer_1_out), .clk(clk), .K(multiplexer_2_out), .Q(out_11), .en(en), .reset(_0));  // open: Qn, preset
  Multiplexer multiplexer_3 (.in0(has_2_k), .in1(conversor_d_jk_2_k), .out(multiplexer_3_out), .sel(load));  // open: en
  Conversor_D_JK conversor_d_jk_2 (.D(in_2), .J(conversor_d_jk_2_j), .K(conversor_d_jk_2_k));
  HAS has_2 (.Op1(op1), .Op0(op0), .Q0(out_12), .CIn(has_3_cout), .J(has_2_j), .K(has_2_k), .COut(has_2_cout));
  Multiplexer multiplexer_4 (.in0(has_2_j), .in1(conversor_d_jk_2_j), .out(multiplexer_4_out), .sel(load));  // open: en
  J_K_Flip_Flop j_k_ff_2 (
    .J(multiplexer_4_out), .clk(clk), .K(multiplexer_3_out), .Q(out_12), .en(en), .reset(_0));  // open: Qn, preset
  Multiplexer multiplexer_5 (.in0(has_3_k), .in1(conversor_d_jk_3_k), .out(multiplexer_5_out), .sel(load));  // open: en
  Conversor_D_JK conversor_d_jk_3 (.D(in_3), .J(conversor_d_jk_3_j), .K(conversor_d_jk_3_k));
  HAS has_3 (.Op1(op1), .Op0(op0), .Q0(out_13), .CIn(op1), .J(has_3_j), .K(has_3_k), .COut(has_3_cout));
  Multiplexer multiplexer_6 (.in0(has_3_j), .in1(conversor_d_jk_3_j), .out(multiplexer_6_out), .sel(load));  // open: en
  J_K_Flip_Flop j_k_ff_3 (
    .J(multiplexer_6_out), .clk(clk), .K(multiplexer_5_out), .Q(out_13), .en(en), .reset(_0));  // open: Qn, preset
endmodule

module Counter_4_Bits (
  input  in_1,
  input  in_2,
  input  in_3,
  input  in_4,
  input  op0,
  input  op1,
  input  load,
  input  clk,
  input  en,
  input  _0,
  output out_11,
  output out_12,
  output out_13,
  output out_14,
  output out_15
);

  wire conversor_d_jk_1_j, conversor_d_jk_1_k, conversor_d_jk_2_j, conversor_d_jk_2_k, conversor_d_jk_3_j,
       conversor_d_jk_3_k, conversor_d_jk_4_j, conversor_d_jk_4_k, has_1_j, has_1_k, has_2_cout, has_2_j,
       has_2_k, has_3_cout, has_3_j, has_3_k, has_4_cout, has_4_j, has_4_k, multiplexer_1_out,
       multiplexer_2_out, multiplexer_3_out, multiplexer_4_out, multiplexer_5_out, multiplexer_6_out,
       multiplexer_7_out, multiplexer_8_out;

  Multiplexer multiplexer_1 (.in0(has_1_k), .in1(conversor_d_jk_1_k), .out(multiplexer_1_out), .sel(load));  // open: en
  Conversor_D_JK conversor_d_jk_1 (.D(in_1), .J(conversor_d_jk_1_j), .K(conversor_d_jk_1_k));
  HAS has_1 (.Op1(op1), .Op0(op0), .Q0(out_12), .CIn(has_2_cout), .J(has_1_j), .K(has_1_k), .COut(out_11));
  Multiplexer multiplexer_2 (.in0(has_1_j), .in1(conversor_d_jk_1_j), .out(multiplexer_2_out), .sel(load));  // open: en
  J_K_Flip_Flop j_k_ff_1 (
    .J(multiplexer_2_out), .clk(clk), .K(multiplexer_1_out), .Q(out_12), .en(en), .reset(_0));  // open: Qn, preset
  Multiplexer multiplexer_3 (.in0(has_2_k), .in1(conversor_d_jk_2_k), .out(multiplexer_3_out), .sel(load));  // open: en
  Conversor_D_JK conversor_d_jk_2 (.D(in_2), .J(conversor_d_jk_2_j), .K(conversor_d_jk_2_k));
  HAS has_2 (.Op1(op1), .Op0(op0), .Q0(out_13), .CIn(has_3_cout), .J(has_2_j), .K(has_2_k), .COut(has_2_cout));
  Multiplexer multiplexer_4 (.in0(has_2_j), .in1(conversor_d_jk_2_j), .out(multiplexer_4_out), .sel(load));  // open: en
  Multiplexer multiplexer_5 (.in0(has_3_k), .in1(conversor_d_jk_3_k), .out(multiplexer_5_out), .sel(load));  // open: en
  J_K_Flip_Flop j_k_ff_2 (
    .J(multiplexer_4_out), .clk(clk), .K(multiplexer_3_out), .Q(out_13), .en(en), .reset(_0));  // open: Qn, preset
  Conversor_D_JK conversor_d_jk_3 (.D(in_3), .J(conversor_d_jk_3_j), .K(conversor_d_jk_3_k));
  HAS has_3 (.Op1(op1), .Op0(op0), .Q0(out_14), .CIn(has_4_cout), .J(has_3_j), .K(has_3_k), .COut(has_3_cout));
  Multiplexer multiplexer_6 (.in0(has_3_j), .in1(conversor_d_jk_3_j), .out(multiplexer_6_out), .sel(load));  // open: en
  J_K_Flip_Flop j_k_ff_3 (
    .J(multiplexer_6_out), .clk(clk), .K(multiplexer_5_out), .Q(out_14), .en(en), .reset(_0));  // open: Qn, preset
  HAS has_4 (.Op1(op1), .Op0(op0), .Q0(out_15), .CIn(op1), .J(has_4_j), .K(has_4_k), .COut(has_4_cout));
  Multiplexer multiplexer_7 (.in0(has_4_k), .in1(conversor_d_jk_4_k), .out(multiplexer_7_out), .sel(load));  // open: en
  Multiplexer multiplexer_8 (.in0(has_4_j), .in1(conversor_d_jk_4_j), .out(multiplexer_8_out), .sel(load));  // open: en
  Conversor_D_JK conversor_d_jk_4 (.D(in_4), .J(conversor_d_jk_4_j), .K(conversor_d_jk_4_k));
  J_K_Flip_Flop j_k_ff_4 (
    .J(multiplexer_8_out), .clk(clk), .K(multiplexer_7_out), .Q(out_15), .en(en), .reset(_0));  // open: Qn, preset
endmodule

module Counter_5_Bits (
  input  in_1,
  input  in_2,
  input  in_3,
  input  in_4,
  input  in_5,
  input  op0,
  input  op1,
  input  load,
  input  clk,
  input  en,
  input  _0,
  output Cout,
  output out_13,
  output out_14,
  output out_15,
  output out_16,
  output out_17
);

  wire conversor_d_jk_1_j, conversor_d_jk_1_k, conversor_d_jk_2_j, conversor_d_jk_2_k, conversor_d_jk_3_j,
       conversor_d_jk_3_k, conversor_d_jk_4_j, conversor_d_jk_4_k, conversor_d_jk_5_j, conversor_d_jk_5_k,
       has_1_j, has_1_k, has_2_cout, has_2_j, has_2_k, has_3_cout, has_3_j, has_3_k, has_4_cout, has_4_j,
       has_4_k, has_5_cout, has_5_j, has_5_k, multiplexer_1_out, multiplexer_2_out, multiplexer_3_out,
       multiplexer_4_out, multiplexer_5_out, multiplexer_6_out, multiplexer_7_out, multiplexer_8_out,
       multiplexer_9_out, multiplexer_10_out;

  HAS has_1 (.Op1(op1), .Op0(op0), .Q0(out_13), .CIn(has_2_cout), .J(has_1_j), .K(has_1_k), .COut(Cout));
  Multiplexer multiplexer_1 (.in0(has_1_j), .in1(conversor_d_jk_1_j), .out(multiplexer_1_out), .sel(load));  // open: en
  Multiplexer multiplexer_2 (.in0(has_1_k), .in1(conversor_d_jk_1_k), .out(multiplexer_2_out), .sel(load));  // open: en
  Conversor_D_JK conversor_d_jk_1 (.D(in_1), .J(conversor_d_jk_1_j), .K(conversor_d_jk_1_k));
  J_K_Flip_Flop j_k_ff_1 (
    .J(multiplexer_1_out), .clk(clk), .K(multiplexer_2_out), .Q(out_13), .en(en), .reset(_0));  // open: Qn, preset
  Multiplexer multiplexer_3 (.in0(has_2_k), .in1(conversor_d_jk_2_k), .out(multiplexer_3_out), .sel(load));  // open: en
  Conversor_D_JK conversor_d_jk_2 (.D(in_2), .J(conversor_d_jk_2_j), .K(conversor_d_jk_2_k));
  HAS has_2 (.Op1(op1), .Op0(op0), .Q0(out_14), .CIn(has_3_cout), .J(has_2_j), .K(has_2_k), .COut(has_2_cout));
  Multiplexer multiplexer_4 (.in0(has_2_j), .in1(conversor_d_jk_2_j), .out(multiplexer_4_out), .sel(load));  // open: en
  J_K_Flip_Flop j_k_ff_2 (
    .J(multiplexer_4_out), .clk(clk), .K(multiplexer_3_out), .Q(out_14), .en(en), .reset(_0));  // open: Qn, preset
  Multiplexer multiplexer_5 (.in0(has_3_k), .in1(conversor_d_jk_3_k), .out(multiplexer_5_out), .sel(load));  // open: en
  Conversor_D_JK conversor_d_jk_3 (.D(in_3), .J(conversor_d_jk_3_j), .K(conversor_d_jk_3_k));
  HAS has_3 (.Op1(op1), .Op0(op0), .Q0(out_15), .CIn(has_4_cout), .J(has_3_j), .K(has_3_k), .COut(has_3_cout));
  Multiplexer multiplexer_6 (.in0(has_3_j), .in1(conversor_d_jk_3_j), .out(multiplexer_6_out), .sel(load));  // open: en
  Multiplexer multiplexer_7 (.in0(has_4_k), .in1(conversor_d_jk_4_k), .out(multiplexer_7_out), .sel(load));  // open: en
  J_K_Flip_Flop j_k_ff_3 (
    .J(multiplexer_6_out), .clk(clk), .K(multiplexer_5_out), .Q(out_15), .en(en), .reset(_0));  // open: Qn, preset
  Conversor_D_JK conversor_d_jk_4 (.D(in_4), .J(conversor_d_jk_4_j), .K(conversor_d_jk_4_k));
  HAS has_4 (.Op1(op1), .Op0(op0), .Q0(out_16), .CIn(has_5_cout), .J(has_4_j), .K(has_4_k), .COut(has_4_cout));
  Multiplexer multiplexer_8 (.in0(has_4_j), .in1(conversor_d_jk_4_j), .out(multiplexer_8_out), .sel(load));  // open: en
  J_K_Flip_Flop j_k_ff_4 (
    .J(multiplexer_8_out), .clk(clk), .K(multiplexer_7_out), .Q(out_16), .en(en), .reset(_0));  // open: Qn, preset
  HAS has_5 (.Op1(op1), .Op0(op0), .Q0(out_17), .CIn(op1), .J(has_5_j), .K(has_5_k), .COut(has_5_cout));
  Multiplexer multiplexer_9 (.in0(has_5_j), .in1(conversor_d_jk_5_j), .out(multiplexer_9_out), .sel(load));  // open: en
  Multiplexer multiplexer_10 (
    .in0(has_5_k), .in1(conversor_d_jk_5_k), .out(multiplexer_10_out), .sel(load));  // open: en
  Conversor_D_JK conversor_d_jk_5 (.D(in_5), .J(conversor_d_jk_5_j), .K(conversor_d_jk_5_k));
  J_K_Flip_Flop j_k_ff_5 (
    .J(multiplexer_9_out), .clk(clk), .K(multiplexer_10_out), .Q(out_17), .en(en), .reset(_0));  // open: Qn, preset
endmodule
