// Logisim project Game.circ as structural Verilog: 6 circuits, main circuit Game
module Game (
  input  in_1
);

  wire button_1_out, clock_1_out;
  wire [1:0] gamecircuit_1_level, gamecircuit_1_lives, joystick_1_x;
  wire [31:0] gamecircuit_1__0, gamecircuit_1__1, gamecircuit_1__2, gamecircuit_1__3, gamecircuit_1__4,
       gamecircuit_1__5, gamecircuit_1__6, gamecircuit_1__7, gamecircuit_1__8, gamecircuit_1__9,
       gamecircuit_1__10, gamecircuit_1__11, gamecircuit_1__12, gamecircuit_1__13, gamecircuit_1__14,
       gamecircuit_1__15, gamecircuit_1__16, gamecircuit_1__17, gamecircuit_1__18, gamecircuit_1__19,
       gamecircuit_1__20, gamecircuit_1__21, gamecircuit_1__22, gamecircuit_1__23, heartlevel_1_r1,
       heartlevel_1_r2, heartlevel_1_r3, heartlevel_1_r4, heartlevel_1_r5, heartlevel_1_r6, heartlevel_1_r7,
       heartlevel_1_r8;

  Clock clock_1 (.out(clock_1_out));
  Button button_1 (.out(button_1_out));
  Joystick #(.bits(2)) joystick_1 (.x(joystick_1_x));  // open: y
  GameCircuit gamecircuit_1 (
    .clk(clock_1_out), .turn_on(in_1), .restart(button_1_out), .joystick_input(joystick_1_x),
    ._0(gamecircuit_1__0), ._1(gamecircuit_1__1), ._2(gamecircuit_1__2), ._3(gamecircuit_1__3),
    ._4(gamecircuit_1__4), ._5(gamecircuit_1__5), ._6(gamecircuit_1__6), ._7(gamecircuit_1__7),
    ._8(gamecircuit_1__8), ._9(gamecircuit_1__9), ._10(gamecircuit_1__10), ._11(gamecircuit_1__11),
    ._12(gamecircuit_1__12), ._13(gamecircuit_1__13), ._14(gamecircuit_1__14), ._15(gamecircuit_1__15),
    ._16(gamecircuit_1__16), ._17(gamecircuit_1__17), ._18(gamecircuit_1__18), ._19(gamecircuit_1__19),
    ._20(gamecircuit_1__20), ._21(gamecircuit_1__21), ._22(gamecircuit_1__22), ._23(gamecircuit_1__23),
    .lives(gamecircuit_1_lives), .level(gamecircuit_1_level));
  HeartLevel heartlevel_1 (
    .lives(gamecircuit_1_lives), .level(gamecircuit_1_level), .R1(heartlevel_1_r1), .R2(heartlevel_1_r2),
    .R3(heartlevel_1_r3), .R4(heartlevel_1_r4), .R5(heartlevel_1_r5), .R6(heartlevel_1_r6),
    .R7(heartlevel_1_r7), .R8(heartlevel_1_r8));
  DotMatrix #(.inputtype("row"), .matrixcols(32), .matrixrows(24)) dotmatrix_1 (
    .row0(gamecircuit_1__0), .row1(gamecircuit_1__1), .row2(gamecircuit_1__2), .row3(gamecircuit_1__3),
    .row4(gamecircuit_1__4), .row5(gamecircuit_1__5), .row6(gamecircuit_1__6), .row7(gamecircuit_1__7),
    .row8(gamecircuit_1__8), .row9(gamecircuit_1__9), .row10(gamecircuit_1__10), .row11(gamecircuit_1__11),
    .row12(gamecircuit_1__12), .row13(gamecircuit_1__13), .row14(gamecircuit_1__14),
    .row15(gamecircuit_1__15), .row16(gamecircuit_1__16), .row17(gamecircuit_1__17),
    .row18(gamecircuit_1__18), .row19(gamecircuit_1__19), .row20(gamecircuit_1__20),
    .row21(gamecircuit_1__21), .row22(gamecircuit_1__22), .row23(gamecircuit_1__23));
  DotMatrix #(.inputtype("row"), .matrixcols(32), .matrixrows(8)) dotmatrix_2 (
    .row0(heartlevel_1_r1), .row1(heartlevel_1_r2), .row2(heartlevel_1_r3), .row3(heartlevel_1_r4),
    .row4(heartlevel_1_r5), .row5(heartlevel_1_r6), .row6(heartlevel_1_r7), .row7(heartlevel_1_r8));
endmodule

module GameCircuit (
  input  clk,
  input  [1:0] joystick_input,
  input  turn_on,
  input  restart,
  output [31:0] _0,
  output [31:0] _1,
  output [31:0] _2,
  output [31:0] _3,
  output [31:0] _4,
  output [31:0] _5,
  output [31:0] _6,
  output [31:0] _7,
  output [31:0] _8,
  output [31:0] _9,
  output [31:0] _10,
  output [31:0] _11,
  output [31:0] _12,
  output [31:0] _13,
  output [31:0] _14,
  output [31:0] _15,
  output [31:0] _16,
  output [31:0] _17,
  output [31:0] _18,
  output [31:0] _19,
  output [31:0] _20,
  output [31:0] _21,
  output [31:0] _22,
  output [31:0] _23,
  output [1:0] lives,
  output [1:0] level
);

  wire and_1_out, and_2_out, collision_1_collision, comparator_1_eq, comparator_2_eq, comparator_3_eq,
       createenablelogic_1_enable, createenablelogic_1_reset_counters, gamelogic_1_game_loop_s0,
       gamelogic_1_game_loop_s1, gamelogic_1_game_loop_s2, not_1_out, or_1_out, or_2_out, or_3_out, or_4_out,
       or_5_out, waitlogic_1_en_car_counter, waitlogic_1_en_generator;
  wire [2:0] counter_3_bits_1_out_11;
  wire [3:0] counter_4_bits_1_out_15;
  wire [4:0] player_input_processor_1_r0, player_input_processor_1_r0_2, player_input_processor_1_r1,
       player_input_processor_1_r2, player_input_processor_1_r2_2, player_input_processor_1_r2_3,
       player_input_processor_1_r3;
  wire [31:0] array_12_32_bits_2_out_13, array_12_32_bits_2_out_14, array_12_32_bits_2_out_15,
       array_12_32_bits_2_out_16, generator_1_out_5;

  waitLogic waitlogic_1 (
    .start(createenablelogic_1_enable), .car_created(comparator_1_eq),
    .en_car_counter(waitlogic_1_en_car_counter), .en_generator(waitlogic_1_en_generator));
  GameLogic gamelogic_1 (
    .clk(clk), .start(createenablelogic_1_enable), .r_start(or_1_out), .cycle_counter_end(comparator_2_eq),
    .game_loop_s0(gamelogic_1_game_loop_s0), .game_loop_s1(gamelogic_1_game_loop_s1),
    .game_loop_s2(gamelogic_1_game_loop_s2));
  or or_1 (or_1_out, collision_1_collision, restart);
  and and_1 (and_1_out, waitlogic_1_en_generator, gamelogic_1_game_loop_s2);
  and and_2 (and_2_out, waitlogic_1_en_car_counter, gamelogic_1_game_loop_s2);
  Counter_4_Bits counter_4_bits_1 (
    .op0(1'b0), .op1(1'b1), .load(1'b0), .clk(clk), .en(gamelogic_1_game_loop_s2),
    ._0(gamelogic_1_game_loop_s1), .in_1(1'b0), .in_2(1'b0), .in_3(1'b0), .in_4(1'b0),
    .out_12(counter_4_bits_1_out_15[3]), .out_13(counter_4_bits_1_out_15[2]),
    .out_14(counter_4_bits_1_out_15[1]), .out_15(counter_4_bits_1_out_15[0]));  // open: out_11
  CreateEnableLogic createenablelogic_1 (
    .turn_on(turn_on), .restart(restart), .alive(not_1_out), .enable(createenablelogic_1_enable),
    .reset_counters(createenablelogic_1_reset_counters));
  Counter_3_Bits counter_3_bits_1 (
    .op0(1'b0), .op1(1'b1), .load(1'b0), .clk(clk), .en(and_2_out), ._0(gamelogic_1_game_loop_s1),
    .in_1(1'b0), .in_2(1'b0), .in_3(1'b0), .out_11(counter_3_bits_1_out_11[2]),
    .out_12(counter_3_bits_1_out_11[1]), .out_13(counter_3_bits_1_out_11[0]));  // open: out_10
  Comparator #(.width(3)) comparator_1 (.a(counter_3_bits_1_out_11), .b(3'b100), .eq(comparator_1_eq));  // open: gt, lt
  Comparator #(.width(4)) comparator_2 (
    .a(counter_4_bits_1_out_15), .b(4'b1001), .eq(comparator_2_eq));  // open: gt, lt
  or or_2 (or_2_out, collision_1_collision, createenablelogic_1_reset_counters);
  Generator generator_1 (
    .en(and_1_out), .clk(clk), .\generate (gamelogic_1_game_loop_s1),
    .car_part(counter_3_bits_1_out_11[1:0]), .out_5(generator_1_out_5));
  or or_3 (or_3_out, gamelogic_1_game_loop_s1, gamelogic_1_game_loop_s2);
  Counter_2_Bits counter_2_bits_1 (
    .op0(1'b1), .op1(1'b1), .load(createenablelogic_1_reset_counters), .clk(clk), .en(or_2_out), ._0(1'b0),
    .in_1(1'b1), .in_2(1'b1), .out_10(lives[1]), .out_11(lives[0]));  // open: out_9
  Counter_2_Bits counter_2_bits_2 (
    .op0(1'b0), .op1(1'b1), .load(createenablelogic_1_reset_counters), .clk(clk), .en(or_2_out), ._0(1'b0),
    .in_1(1'b0), .in_2(1'b1), .out_10(level[1]), .out_11(level[0]));  // open: out_9
  Array_12_32_Bits array_12_32_bits_1 (
    .Value(generator_1_out_5), .Op(or_3_out), .Clk(clk), ._0(gamelogic_1_game_loop_s0), .out_5(_0),
    .out_6(_1), .out_7(_2), .out_8(_3), .out_9(_4), .out_10(_5), .out_11(_6), .out_12(_7), .out_13(_8),
    .out_14(_9), .out_15(_10), .out_16(_11));
  Array_12_32_Bits array_12_32_bits_2 (
    .Value(_11), .Op(or_3_out), .Clk(clk), ._0(gamelogic_1_game_loop_s0), .out_5(_12), .out_6(_13),
    .out_7(_14), .out_8(_15), .out_9(_16), .out_10(_17), .out_11(_18), .out_12(_19),
    .out_13(array_12_32_bits_2_out_13), .out_14(array_12_32_bits_2_out_14),
    .out_15(array_12_32_bits_2_out_15), .out_16(array_12_32_bits_2_out_16));
  or or_4 (or_4_out, gamelogic_1_game_loop_s0, gamelogic_1_game_loop_s1, gamelogic_1_game_loop_s2);
  or or_5 (or_5_out, gamelogic_1_game_loop_s1, gamelogic_1_game_loop_s2);
  Comparator #(.width(2)) comparator_3 (.a(lives), .b(2'b00), .eq(comparator_3_eq));  // open: gt, lt
  not not_1 (not_1_out, comparator_3_eq);
  Collision collision_1 (
    ._20(array_12_32_bits_2_out_13), ._21(array_12_32_bits_2_out_14), ._22(array_12_32_bits_2_out_15),
    ._23(array_12_32_bits_2_out_16), .R3(player_input_processor_1_r3), .R2(player_input_processor_1_r2),
    .R2_2(player_input_processor_1_r2_3), .R1(player_input_processor_1_r1), .R0(player_input_processor_1_r0),
    .R0_2(player_input_processor_1_r0_2), .collision(collision_1_collision));
  Player_Input_Processor player_input_processor_1 (
    .load(gamelogic_1_game_loop_s0), .clk(clk), .en(or_4_out), .Input(joystick_input),
    .R3(player_input_processor_1_r3), .R2(player_input_processor_1_r2), .R2_2(player_input_processor_1_r2_2),
    .R2_3(player_input_processor_1_r2_3), .R1(player_input_processor_1_r1), .R0(player_input_processor_1_r0),
    .R0_2(player_input_processor_1_r0_2));  // open: _0
  Merge_Player_Input merge_player_input_1 (
    ._20(array_12_32_bits_2_out_13), ._21(array_12_32_bits_2_out_14), ._22(array_12_32_bits_2_out_15),
    ._23(array_12_32_bits_2_out_16), .en(or_5_out), .R3(player_input_processor_1_r3),
    .R2(player_input_processor_1_r2), .R2_2(player_input_processor_1_r2_2),
    .R2_3(player_input_processor_1_r2_3), .R1(player_input_processor_1_r1), .R0(player_input_processor_1_r0),
    .R0_2(player_input_processor_1_r0_2), ._20_2(_20), ._21_2(_21), ._22_2(_22), ._23_2(_23));
endmodule

module GameLogicCircuit (
  input  Q1,
  input  Q0,
  input  start,
  input  r_start,
  input  cycle_counter_end,
  output D1,
  output D0,
  output game_loop_s0,
  output game_loop_s1,
  output game_loop_s2
);

  wire and_1_out, and_2_out, and_3_out, and_4_out, and_5_out, and_6_out, and_7_out, and_8_out, and_9_out,
       and_10_out, and_11_out, and_12_out, not_1_out, not_2_out, not_3_out, not_4_out, not_5_out, not_6_out,
       not_7_out, not_8_out, not_9_out, not_10_out, not_11_out, not_12_out;

  not not_1 (not_1_out, r_start);
  not not_2 (not_2_out, r_start);
  not not_3 (not_3_out, cycle_counter_end);
  not not_4 (not_4_out, Q1);
  not not_5 (not_5_out, Q0);
  not not_6 (not_6_out, r_start);
  not not_7 (not_7_out, Q0);
  not not_8 (not_8_out, r_start);
  not not_9 (not_9_out, Q1);
  not not_10 (not_10_out, Q0);
  not not_11 (not_11_out, r_start);
  not not_12 (not_12_out, r_start);
  and and_1 (and_1_out, Q0, start, not_1_out);
  and and_2 (and_2_out, Q1, start, not_2_out, not_3_out);
  and and_3 (and_3_out, Q1, Q0);
  and and_4 (and_4_out, not_4_out, not_5_out, start, not_6_out);
  and and_5 (and_5_out, not_7_out, start, not_8_out, cycle_counter_end);
  and and_6 (and_6_out, Q1, Q0);
  and and_7 (and_7_out, not_9_out, not_10_out);
  and and_8 (and_8_out, Q1, Q0);
  and and_9 (and_9_out, Q0, start, not_11_out);
  and and_10 (and_10_out, Q1, Q0);
  and and_11 (and_11_out, Q1, start, not_12_out);
  and and_12 (and_12_out, Q1, Q0);
  or or_1 (D1, and_1_out, and_2_out, and_3_out);
  or or_2 (D0, and_4_out, and_5_out, and_6_out);
  or or_3 (game_loop_s0, and_7_out, and_8_out);
  or or_4 (game_loop_s1, and_9_out, and_10_out);
  or or_5 (game_loop_s2, and_11_out, and_12_out);
endmodule

module GameLogic (
  input  clk,
  input  start,
  input  r_start,
  input  cycle_counter_end,
  output game_loop_s0,
  output game_loop_s1,
  output game_loop_s2
);

  wire d_ff_1_q, d_ff_2_q, gamelogiccircuit_1_d0, gamelogiccircuit_1_d1;

  GameLogicCircuit gamelogiccircuit_1 (
    .Q1(d_ff_1_q), .Q0(d_ff_2_q), .start(start), .r_start(r_start), .cycle_counter_end(cycle_counter_end),
    .D1(gamelogiccircuit_1_d1), .D0(gamelogiccircuit_1_d0), .game_loop_s0(game_loop_s0),
    .game_loop_s1(game_loop_s1), .game_loop_s2(game_loop_s2));
  D_Flip_Flop d_ff_1 (.clk(clk), .D(gamelogiccircuit_1_d1), .Q(d_ff_1_q));  // open: Qn, preset, en, reset
  D_Flip_Flop d_ff_2 (.clk(clk), .D(gamelogiccircuit_1_d0), .Q(d_ff_2_q));  // open: Qn, preset, en, reset
endmodule

module CreateEnableLogic (
  input  turn_on,
  input  restart,
  input  alive,
  output enable,
  output reset_counters
);

  wire and_1_out, and_2_out;

  and and_1 (and_1_out, turn_on, alive);
  and and_2 (and_2_out, turn_on, restart);
  and and_3 (reset_counters, turn_on, restart);
  or or_1 (enable, and_1_out, and_2_out);
endmodule

module waitLogic (
  input  start,
  input  car_created,
  output en_car_counter,
  output en_generator
);

  wire not_1_out, not_2_out;

  not not_1 (not_1_out, car_created);
  not not_2 (not_2_out, car_created);
  and and_1 (en_car_counter, start, not_1_out);
  and and_2 (en_generator, start, not_2_out);
endmodule
