// Logisim project GameUpdate.circ as structural Verilog: 3 circuits, main circuit Collision
module Collision (
  input  [4:0] R3,
  input  [31:0] _20,
  input  [4:0] R2,
  input  [31:0] _21,
  input  [4:0] R2_2,
  input  [4:0] R1,
  input  [31:0] _22,
  input  [4:0] R0,
  input  [31:0] _23,
  input  [4:0] R0_2,
  output collision
);

  wire bitselector_1_out, bitselector_2_out, bitselector_3_out, bitselector_4_out, bitselector_5_out,
       bitselector_6_out;

  BitSelector #(.width(32)) bitselector_1 (.in(_20), .out(bitselector_1_out), .sel(R3));
  BitSelector #(.width(32)) bitselector_2 (.in(_21), .out(bitselector_2_out), .sel(R2));
  BitSelector #(.width(32)) bitselector_3 (.in(_21), .out(bitselector_3_out), .sel(R2_2));
  BitSelector #(.width(32)) bitselector_4 (.in(_22), .out(bitselector_4_out), .sel(R1));
  BitSelector #(.width(32)) bitselector_5 (.in(_23), .out(bitselector_5_out), .sel(R0));
  BitSelector #(.width(32)) bitselector_6 (.in(_23), .out(bitselector_6_out), .sel(R0_2));
  or or_1 (collision, bitselector_1_out, bitselector_2_out, bitselector_3_out, bitselector_4_out, bitselector_5_out, bitselector_6_out);
endmodule

module Convert_To_Matrix_Form (
  input  [4:0] in_1,
  input  [4:0] in_2,
  input  [4:0] in_3,
  input  [4:0] in_4,
  input  [4:0] in_5,
  input  [4:0] in_6,
  input  [4:0] in_7,
  output [31:0] out_8,
  output [31:0] out_9,
  output [31:0] out_10,
  output [31:0] out_11,
  output [31:0] out_12,
  output [31:0] out_13,
  output [31:0] out_14
);

  Decoder #(.select(5)) decoder_1 (
    .out0(out_8[0]), .out1(out_8[1]), .out2(out_8[2]), .out3(out_8[3]), .out4(out_8[4]), .out5(out_8[5]),
    .out6(out_8[6]), .out7(out_8[7]), .out8(out_8[8]), .out9(out_8[9]), .out10(out_8[10]), .out11(out_8[11]),
    .out12(out_8[12]), .out13(out_8[13]), .out14(out_8[14]), .out15(out_8[15]), .out16(out_8[16]),
    .out17(out_8[17]), .out18(out_8[18]), .out19(out_8[19]), .out20(out_8[20]), .out21(out_8[21]),
    .out22(out_8[22]), .out23(out_8[23]), .out24(out_8[24]), .out25(out_8[25]), .out26(out_8[26]),
    .out27(out_8[27]), .out28(out_8[28]), .out29(out_8[29]), .out30(out_8[30]), .out31(out_8[31]), .sel(in_1));  // open: en
  Decoder #(.select(5)) decoder_2 (
    .out0(out_9[0]), .out1(out_9[1]), .out2(out_9[2]), .out3(out_9[3]), .out4(out_9[4]), .out5(out_9[5]),
    .out6(out_9[6]), .out7(out_9[7]), .out8(out_9[8]), .out9(out_9[9]), .out10(out_9[10]), .out11(out_9[11]),
    .out12(out_9[12]), .out13(out_9[13]), .out14(out_9[14]), .out15(out_9[15]), .out16(out_9[16]),
    .out17(out_9[17]), .out18(out_9[18]), .out19(out_9[19]), .out20(out_9[20]), .out21(out_9[21]),
    .out22(out_9[22]), .out23(out_9[23]), .out24(out_9[24]), .out25(out_9[25]), .out26(out_9[26]),
    .out27(out_9[27]), .out28(out_9[28]), .out29(out_9[29]), .out30(out_9[30]), .out31(out_9[31]), .sel(in_2));  // open: en
  Decoder #(.select(5)) decoder_3 (
    .out0(out_10[0]), .out1(out_10[1]), .out2(out_10[2]), .out3(out_10[3]), .out4(out_10[4]),
    .out5(out_10[5]), .out6(out_10[6]), .out7(out_10[7]), .out8(out_10[8]), .out9(out_10[9]),
    .out10(out_10[10]), .out11(out_10[11]), .out12(out_10[12]), .out13(out_10[13]), .out14(out_10[14]),
    .out15(out_10[15]), .out16(out_10[16]), .out17(out_10[17]), .out18(out_10[18]), .out19(out_10[19]),
    .out20(out_10[20]), .out21(out_10[21]), .out22(out_10[22]), .out23(out_10[23]), .out24(out_10[24]),
    .out25(out_10[25]), .out26(out_10[26]), .out27(out_10[27]), .out28(out_10[28]), .out29(out_10[29]),
    .out30(out_10[30]), .out31(out_10[31]), .sel(in_3));  // open: en
  Decoder #(.select(5)) decoder_4 (
    .out0(out_11[0]), .out1(out_11[1]), .out2(out_11[2]), .out3(out_11[3]), .out4(out_11[4]),
    .out5(out_11[5]), .out6(out_11[6]), .out7(out_11[7]), .out8(out_11[8]), .out9(out_11[9]),
    .out10(out_11[10]), .out11(out_11[11]), .out12(out_11[12]), .out13(out_11[13]), .out14(out_11[14]),
    .out15(out_11[15]), .out16(out_11[16]), .out17(out_11[17]), .out18(out_11[18]), .out19(out_11[19]),
    .out20(out_11[20]), .out21(out_11[21]), .out22(out_11[22]), .out23(out_11[23]), .out24(out_11[24]),
    .out25(out_11[25]), .out26(out_11[26]), .out27(out_11[27]), .out28(out_11[28]), .out29(out_11[29]),
    .out30(out_11[30]), .out31(out_11[31]), .sel(in_4));  // open: en
  Decoder #(.select(5)) decoder_5 (
    .out0(out_12[0]), .out1(out_12[1]), .out2(out_12[2]), .out3(out_12[3]), .out4(out_12[4]),
    .out5(out_12[5]), .out6(out_12[6]), .out7(out_12[7]), .out8(out_12[8]), .out9(out_12[9]),
    .out10(out_12[10]), .out11(out_12[11]), .out12(out_12[12]), .out13(out_12[13]), .out14(out_12[14]),
    .out15(out_12[15]), .out16(out_12[16]), .out17(out_12[17]), .out18(out_12[18]), .out19(out_12[19]),
    .out20(out_12[20]), .out21(out_12[21]), .out22(out_12[22]), .out23(out_12[23]), .out24(out_12[24]),
    .out25(out_12[25]), .out26(out_12[26]), .out27(out_12[27]), .out28(out_12[28]), .out29(out_12[29]),
    .out30(out_12[30]), .out31(out_12[31]), .sel(in_5));  // open: en
  Decoder #(.select(5)) decoder_6 (
    .out0(out_13[0]), .out1(out_13[1]), .out2(out_13[2]), .out3(out_13[3]), .out4(out_13[4]),
    .out5(out_13[5]), .out6(out_13[6]), .out7(out_13[7]), .out8(out_13[8]), .out9(out_13[9]),
    .out10(out_13[10]), .out11(out_13[11]), .out12(out_13[12]), .out13(out_13[13]), .out14(out_13[14]),
    .out15(out_13[15]), .out16(out_13[16]), .out17(out_13[17]), .out18(out_13[18]), .out19(out_13[19]),
    .out20(out_13[20]), .out21(out_13[21]), .out22(out_13[22]), .out23(out_13[23]), .out24(out_13[24]),
    .out25(out_13[25]), .out26(out_13[26]), .out27(out_13[27]), .out28(out_13[28]), .out29(out_13[29]),
    .out30(out_13[30]), .out31(out_13[31]), .sel(in_6));  // open: en
  Decoder #(.select(5)) decoder_7 (
    .out0(out_14[0]), .out1(out_14[1]), .out2(out_14[2]), .out3(out_14[3]), .out4(out_14[4]),
    .out5(out_14[5]), .out6(out_14[6]), .out7(out_14[7]), .out8(out_14[8]), .out9(out_14[9]),
    .out10(out_14[10]), .out11(out_14[11]), .out12(out_14[12]), .out13(out_14[13]), .out14(out_14[14]),
    .out15(out_14[15]), .out16(out_14[16]), .out17(out_14[17]), .out18(out_14[18]), .out19(out_14[19]),
    .out20(out_14[20]), .out21(out_14[21]), .out22(out_14[22]), .out23(out_14[23]), .out24(out_14[24]),
    .out25(out_14[25]), .out26(out_14[26]), .out27(out_14[27]), .out28(out_14[28]), .out29(out_14[29]),
    .out30(out_14[30]), .out31(out_14[31]), .sel(in_7));  // open: en
endmodule

module Merge_Player_Input (
  input  [4:0] R3,
  input  [4:0] R2,
  input  [4:0] R2_2,
  input  [4:0] R2_3,
  input  [4:0] R1,
  input  [4:0] R0,
  input  [4:0] R0_2,
  input  [31:0] _20,
  input  [31:0] _21,
  input  [31:0] _22,
  input  [31:0] _23,
  input  en,
  output [31:0] _20_2,
  output [31:0] _21_2,
  output [31:0] _22_2,
  output [31:0] _23_2
);

  wire [31:0] convert_to_matrix_form_1_out_8, convert_to_matrix_form_1_out_9,
       convert_to_matrix_form_1_out_10, convert_to_matrix_form_1_out_11, convert_to_matrix_form_1_out_12,
       convert_to_matrix_form_1_out_13, convert_to_matrix_form_1_out_14, or_1_out, or_2_out, or_3_out,
       or_4_out, or_5_out, or_6_out;

  assign or_1_out = convert_to_matrix_form_1_out_14 | _20;  // OR_Gate or_1, 32 bits wide
  assign or_2_out = or_3_out | _21;  // OR_Gate or_2, 32 bits wide
  assign or_3_out = convert_to_matrix_form_1_out_13 | convert_to_matrix_form_1_out_12 | convert_to_matrix_form_1_out_11;  // OR_Gate or_3, 32 bits wide
  assign or_4_out = convert_to_matrix_form_1_out_10 | _22;  // OR_Gate or_4, 32 bits wide
  assign or_5_out = or_6_out | _23;  // OR_Gate or_5, 32 bits wide
  Multiplexer #(.width(32)) multiplexer_1 (.in0(_20), .in1(or_1_out), .out(_20_2), .sel(en));  // open: en
  Multiplexer #(.width(32)) multiplexer_2 (.in0(_21), .in1(or_2_out), .out(_21_2), .sel(en));  // open: en
  Multiplexer #(.width(32)) multiplexer_3 (.in0(_22), .in1(or_4_out), .out(_22_2), .sel(en));  // open: en
  Convert_To_Matrix_Form convert_to_matrix_form_1 (
    .in_1(R0_2), .in_2(R0), .in_3(R1), .in_4(R2_3), .in_5(R2_2), .in_6(R2), .in_7(R3),
    .out_8(convert_to_matrix_form_1_out_8), .out_9(convert_to_matrix_form_1_out_9),
    .out_10(convert_to_matrix_form_1_out_10), .out_11(convert_to_matrix_form_1_out_11),
    .out_12(convert_to_matrix_form_1_out_12), .out_13(convert_to_matrix_form_1_out_13),
    .out_14(convert_to_matrix_form_1_out_14));
  assign or_6_out = convert_to_matrix_form_1_out_9 | convert_to_matrix_form_1_out_8;  // OR_Gate or_6, 32 bits wide
  Multiplexer #(.width(32)) multiplexer_4 (.in0(_23), .in1(or_5_out), .out(_23_2), .sel(en));  // open: en
endmodule
