// Logisim project Live-Level.circ as structural Verilog: 1 circuit, main circuit HeartLevel
module HeartLevel (
  input  [1:0] lives,
  input  [1:0] level,
  output [31:0] R1,
  output [31:0] R2,
  output [31:0] R3,
  output [31:0] R4,
  output [31:0] R5,
  output [31:0] R6,
  output [31:0] R7,
  output [31:0] R8
);

  wire [31:0] multiplexer_1_out, multiplexer_2_out, multiplexer_3_out, multiplexer_4_out, multiplexer_5_out,
       multiplexer_6_out, multiplexer_7_out, multiplexer_8_out, multiplexer_9_out, multiplexer_10_out;

  Multiplexer #(.select(2), .width(32)) multiplexer_1 (
    .in0(32'h380000), .in1(32'h80000), .in2(32'h380000), .in3(32'h380000), .out(multiplexer_1_out),
    .sel(lives));  // open: en
  assign R3 = multiplexer_1_out | 32'h6c000200 | multiplexer_6_out;  // OR_Gate or_1, 32 bits wide
  Multiplexer #(.select(2), .width(32)) multiplexer_2 (
    .in0(32'h280000), .in1(32'h180000), .in2(32'h80000), .in3(32'h80000), .out(multiplexer_2_out), .sel(lives));  // open: en
  assign R4 = multiplexer_2_out | 32'h7c800220 | multiplexer_7_out;  // OR_Gate or_2, 32 bits wide
  Multiplexer #(.select(2), .width(32)) multiplexer_3 (
    .in0(32'h280000), .in1(32'h80000), .in2(32'h380000), .in3(32'h380000), .out(multiplexer_3_out),
    .sel(lives));  // open: en
  assign R5 = multiplexer_3_out | 32'h7c000200 | multiplexer_8_out;  // OR_Gate or_3, 32 bits wide
  Multiplexer #(.select(2), .width(32)) multiplexer_4 (
    .in0(32'h280000), .in1(32'h80000), .in2(32'h200000), .in3(32'h80000), .out(multiplexer_4_out), .sel(lives));  // open: en
  assign R6 = multiplexer_4_out | 32'h38800220 | multiplexer_9_out;  // OR_Gate or_4, 32 bits wide
  Multiplexer #(.select(2), .width(32)) multiplexer_5 (
    .in0(32'h380000), .in1(32'h80000), .in2(32'h380000), .in3(32'h380000), .out(multiplexer_5_out),
    .sel(lives));  // open: en
  assign R7 = multiplexer_5_out | 32'h10000380 | multiplexer_10_out;  // OR_Gate or_5, 32 bits wide
  Multiplexer #(.select(2), .width(32)) multiplexer_6 (
    .in0(32'he), .in1(32'h2), .in2(32'he), .in3(32'he), .out(multiplexer_6_out), .sel(level));  // open: en
  Multiplexer #(.select(2), .width(32)) multiplexer_7 (
    .in0(32'ha), .in1(32'h6), .in2(32'h2), .in3(32'h2), .out(multiplexer_7_out), .sel(level));  // open: en
  Multiplexer #(.select(2), .width(32)) multiplexer_8 (
    .in0(32'ha), .in1(32'h2), .in2(32'he), .in3(32'he), .out(multiplexer_8_out), .sel(level));  // open: en
  Multiplexer #(.select(2), .width(32)) multiplexer_9 (
    .in0(32'ha), .in1(32'h2), .in2(32'h8), .in3(32'h2), .out(multiplexer_9_out), .sel(level));  // open: en
  Multiplexer #(.select(2), .width(32)) multiplexer_10 (
    .in0(32'he), .in1(32'h2), .in2(32'he), .in3(32'he), .out(multiplexer_10_out), .sel(level));  // open: en

  assign R1 = {32{1'b0}};
  assign R2 = 32'h6c000200;
  assign R8 = {32{1'b0}};
endmodule
