// Logisim project Player.circ as structural Verilog: 2 circuits, main circuit Player-Input-Processor
module Player_Input_Processor (
  input  [1:0] Input,
  input  load,
  input  clk,
  input  en,
  input  _0,
  output [4:0] R3,
  output [4:0] R2,
  output [4:0] R2_2,
  output [4:0] R2_3,
  output [4:0] R1,
  output [4:0] R0,
  output [4:0] R0_2
);

  wire input_encoder_1_c0, input_encoder_1_c1;

  Input_Encoder input_encoder_1 (.D0(Input[0]), .D1(Input[1]), .C1(input_encoder_1_c1), .C0(input_encoder_1_c0));
  Counter_5_Bits counter_5_bits_1 (
    .op0(input_encoder_1_c0), .op1(input_encoder_1_c1), .load(load), .clk(clk), .en(en), ._0(_0),
    .in_1(1'b0), .in_2(1'b1), .in_3(1'b1), .in_4(1'b1), .in_5(1'b1), .out_13(R3[4]), .out_14(R3[3]),
    .out_15(R3[2]), .out_16(R3[1]), .out_17(R3[0]));  // open: Cout
  Counter_5_Bits counter_5_bits_2 (
    .op0(input_encoder_1_c0), .op1(input_encoder_1_c1), .load(load), .clk(clk), .en(en), ._0(_0),
    .in_1(1'b0), .in_2(1'b1), .in_3(1'b1), .in_4(1'b1), .in_5(1'b0), .out_13(R2[4]), .out_14(R2[3]),
    .out_15(R2[2]), .out_16(R2[1]), .out_17(R2[0]));  // open: Cout
  Counter_5_Bits counter_5_bits_3 (
    .op0(input_encoder_1_c0), .op1(input_encoder_1_c1), .load(load), .clk(clk), .en(en), ._0(_0),
    .in_1(1'b0), .in_2(1'b1), .in_3(1'b1), .in_4(1'b1), .in_5(1'b1), .out_13(R2_2[4]), .out_14(R2_2[3]),
    .out_15(R2_2[2]), .out_16(R2_2[1]), .out_17(R2_2[0]));  // open: Cout
  Counter_5_Bits counter_5_bits_4 (
    .op0(input_encoder_1_c0), .op1(input_encoder_1_c1), .load(load), .clk(clk), .en(en), ._0(_0),
    .in_1(1'b1), .in_2(1'b0), .in_3(1'b0), .in_4(1'b0), .in_5(1'b0), .out_13(R2_3[4]), .out_14(R2_3[3]),
    .out_15(R2_3[2]), .out_16(R2_3[1]), .out_17(R2_3[0]));  // open: Cout
  Counter_5_Bits counter_5_bits_5 (
    .op0(input_encoder_1_c0), .op1(input_encoder_1_c1), .load(load), .clk(clk), .en(en), ._0(_0),
    .in_1(1'b0), .in_2(1'b1), .in_3(1'b1), .in_4(1'b1), .in_5(1'b1), .out_13(R1[4]), .out_14(R1[3]),
    .out_15(R1[2]), .out_16(R1[1]), .out_17(R1[0]));  // open: Cout
  Counter_5_Bits counter_5_bits_6 (
    .op0(input_encoder_1_c0), .op1(input_encoder_1_c1), .load(load), .clk(clk), .en(en), ._0(_0),
    .in_1(1'b0), .in_2(1'b1), .in_3(1'b1), .in_4(1'b1), .in_5(1'b0), .out_13(R0[4]), .out_14(R0[3]),
    .out_15(R0[2]), .out_16(R0[1]), .out_17(R0[0]));  // open: Cout
  Counter_5_Bits counter_5_bits_7 (
    .op0(input_encoder_1_c0), .op1(input_encoder_1_c1), .load(load), .clk(clk), .en(en), ._0(_0),
    .in_1(1'b1), .in_2(1'b0), .in_3(1'b0), .in_4(1'b0), .in_5(1'b0), .out_13(R0_2[4]), .out_14(R0_2[3]),
    .out_15(R0_2[2]), .out_16(R0_2[1]), .out_17(R0_2[0]));  // open: Cout
endmodule

module Input_Encoder (
  input  D0,
  input  D1,
  output C1,
  output C0
);


  assign C0 = D1;
  assign C1 = D0;
endmodule
