// Logisim project ShiftRegister.circ as structural Verilog: 2 circuits, main circuit Array-4-32-Bits
module Array_4_32_Bits (
  input  [31:0] Value,
  input  Op,
  input  Clk,
  input  _0,
  output [31:0] out_5,
  output [31:0] out_6,
  output [31:0] out_7,
  output [31:0] out_8
);

  wire [31:0] multiplexer_1_out, multiplexer_2_out, multiplexer_3_out, multiplexer_4_out;

  Multiplexer #(.width(32)) multiplexer_1 (.in0(out_5), .in1(Value), .out(multiplexer_1_out), .sel(Op));  // open: en
  Multiplexer #(.width(32)) multiplexer_2 (.in0(out_6), .in1(out_5), .out(multiplexer_2_out), .sel(Op));  // open: en
  Register #(.width(32)) register_1 (.D(multiplexer_1_out), .Q(out_5), .clk(Clk), .clr(_0));  // open: en
  Multiplexer #(.width(32)) multiplexer_3 (.in0(out_7), .in1(out_6), .out(multiplexer_3_out), .sel(Op));  // open: en
  Register #(.width(32)) register_2 (.D(multiplexer_2_out), .Q(out_6), .clk(Clk), .clr(_0));  // open: en
  Register #(.width(32)) register_3 (.D(multiplexer_3_out), .Q(out_7), .clk(Clk), .clr(_0));  // open: en
  Multiplexer #(.width(32)) multiplexer_4 (.in0(out_8), .in1(out_7), .out(multiplexer_4_out), .sel(Op));  // open: en
  Register #(.width(32)) register_4 (.D(multiplexer_4_out), .Q(out_8), .clk(Clk), .clr(_0));  // open: en
endmodule

module Array_12_32_Bits (
  input  [31:0] Value,
  input  Op,
  input  Clk,
  input  _0,
  output [31:0] out_5,
  output [31:0] out_6,
  output [31:0] out_7,
  output [31:0] out_8,
  output [31:0] out_9,
  output [31:0] out_10,
  output [31:0] out_11,
  output [31:0] out_12,
  output [31:0] out_13,
  output [31:0] out_14,
  output [31:0] out_15,
  output [31:0] out_16
);

  Array_4_32_Bits array_4_32_bits_1 (
    .Value(Value), .Op(Op), .Clk(Clk), ._0(_0), .out_5(out_5), .out_6(out_6), .out_7(out_7), .out_8(out_8));
  Array_4_32_Bits array_4_32_bits_2 (
    .Value(out_8), .Op(Op), .Clk(Clk), ._0(_0), .out_5(out_9), .out_6(out_10), .out_7(out_11), .out_8(out_12));
  Array_4_32_Bits array_4_32_bits_3 (
    .Value(out_12), .Op(Op), .Clk(Clk), ._0(_0), .out_5(out_13), .out_6(out_14), .out_7(out_15),
    .out_8(out_16));
endmodule
